# Fritzing sketch sketch (saved by Fritzing 0.9.3b)
breadboards: 1

parts:
  S1 = Pushbutton [package="[THT]"]
  S2 = Pushbutton [package="[THT]"]
  S3 = Pushbutton [package="[THT]"]
  S4 = Pushbutton [package="[THT]"]
  Componente1 = Arduino Uno (Rev3)
  J1 = Piezo Speaker
  LED1 = smd LED [color="Red (633nm)" package="0603 [SMD]"]
  LED2 = smd LED [color="Green (565nm)" package="0603 [SMD]"]
  LED3 = smd LED [color="Yellow (595nm)" package="0603 [SMD]"]
  LED4 = smd LED [color="White (4500K)" package="0603 [SMD]"]
  R1 = Resistor [tolerance=±5% resistance=2.2k package=THT]
  R3 = Resistor [tolerance=±5% resistance=2.2k package=THT]
  R4 = Resistor [tolerance=±5% resistance=2.2k package=THT]
  R5 = Resistor [tolerance=±5% resistance=2.2k package=THT]
  R6 = Resistor [tolerance=±5% resistance=2.2k package=THT]
  R7 = Resistor [tolerance=±5% resistance=2.2k package=THT]
  R8 = Resistor [tolerance=±5% resistance=2.2k package=THT]
  R9 = Resistor [tolerance=±5% resistance=2.2k package=THT]

nets:
  N1: S1.Pin_1, S1.Pin_2, S2.Pin_1, S2.Pin_2, S3.Pin_1, S3.Pin_2, S4.Pin_1, S4.Pin_2, Componente1.5V
  N2: S1.Pin_3, S1.Pin_4, Componente1.D5_PWM, R4.Pin_0
  N3: S2.Pin_3, S2.Pin_4, Componente1.D4, R3.Pin_0
  N4: S3.Pin_3, S3.Pin_4, Componente1.D3_PWM, R9.Pin_0
  N5: S4.Pin_3, S4.Pin_4, Componente1.D2, R1.Pin_0
  N6: Componente1.D8, LED1.anode
  N7: Componente1.D9_PWM, LED2.anode
  N8: Componente1.D10_PWM/SS, LED3.anode
  N9: Componente1.D11_PWM/MOSI, LED4.anode
  N10: Componente1.D7, J1.pin2
  N11: Componente1.GND, J1.pin1, R1.Pin_1, R3.Pin_1, R4.Pin_1, R5.Pin_1, R6.Pin_1, R7.Pin_1, R8.Pin_1, R9.Pin_1
  N12: LED1.cathode, R5.Pin_0
  N13: LED2.cathode, R6.Pin_0
  N14: LED3.cathode, R7.Pin_0
  N15: LED4.cathode, R8.Pin_0
